# Fritzing sketch PiBreakoutBoard (saved by Fritzing 0.9.3b)

parts:
  Raspberry_Pi1 = Raspberry Pi 2
  Q1 = Basic FET N-Channel [part_number=IRL540 package="TO220 [THT]"]
  D1 = Schottky Diode [part_number=1N5817 package="300 mil [THT]"]

nets:
  N1: Raspberry_Pi1.GIPO22, Q1.gate
  Wiegand Data 1: Raspberry_Pi1.GIPO13
  Wiegand Data 0: Raspberry_Pi1.GIPO12
  Door Latch -: Q1.drain, D1.anode
  GND: Q1.source
  12V/Door Latch +: D1.cathode
